# Fritzing sketch tennis uno (saved by Fritzing 0.9.3b)
circuit board: 9.2619cm x 8.94461cm
breadboards: 1

parts:
  Bauteil1 = Arduino Uno (Rev3)
  R1 = Resistor [tolerance=±5% resistance=10k package=THT]
  R2 = Resistor [tolerance=±5% resistance=10k package=THT]
  R3 = Resistor [tolerance=±5% resistance=10k package=THT]
  R4 = Resistor [tolerance=±5% resistance=10k package=THT]
  R5 = Resistor [tolerance=±5% resistance=10k package=THT]
  R6 = Resistor [tolerance=±5% resistance=1.2k package=THT]
  R7 = Resistor [tolerance=±5% resistance=1.2k package=THT]
  R8 = Resistor [tolerance=±5% resistance=10k package=THT]
  J1 = Screw terminal - 2 pins [package=THT]
  J4 = male pin header, 11 pins [form="♂ (male)"]
  J3 = male pin header, 8 pins [form="♂ (male)"]

nets:
  N1: Bauteil1.D8, J3.pin7
  N2: Bauteil1.D9_PWM, J3.pin6
  N3: Bauteil1.D10_PWM/SS, J3.pin5
  N4: Bauteil1.D11_PWM/MOSI, J3.pin4
  N5: Bauteil1.D12/MISO, J3.pin3
  N6: Bauteil1.D13/SCK, J4.pin10
  N7: Bauteil1.GND, R1.Pin_0, R2.Pin_0, R3.Pin_0, R4.Pin_0, R5.Pin_0, R6.Pin_0, R7.Pin_0, J1.pin2, J4.pin8, J3.pin2
  N8: Bauteil1.D0/RX, R7.Pin_1, J4.pin7
  N9: Bauteil1.D1/TX, R6.Pin_1, J4.pin6
  N10: Bauteil1.D2, R1.Pin_1, J4.pin5
  N11: Bauteil1.D3_PWM, R2.Pin_1, J4.pin4
  N12: Bauteil1.D4, R3.Pin_1, J4.pin3
  N13: Bauteil1.D5_PWM, R4.Pin_1, J4.pin2
  N14: Bauteil1.D6_PWM, R5.Pin_1, J4.pin1
  N15: Bauteil1.D7, J3.pin8
  N16: Bauteil1.RESET, R8.Pin_0, J4.pin11
  N17: Bauteil1.5V, R8.Pin_1, J4.pin9, J3.pin1
  N18: Bauteil1.VIN, J1.pin1

notes:
  Relaiskarte J3
  Tablau J4
  Stromversorgung J1
